# Fritzing sketch Schema 1 (saved by Fritzing 0.9.3b)

parts:
  SIM868 = FTDI Basic Programmer
  Raspberry_Pi_3 = Raspberry Pi 3 [part_number=RPI-3-V1.2]
  Alarme = Loudspeaker
  3-Axis_Accelerometer1 = 3-Axis Accelerometer Breakout - MMA8452Q
  U1 = TRANSISTOR_NPN_2 [package=to-92]
  R1 = Resistor [tolerance=±5% resistance=10k package="2010 [SMD]"]

nets:
  N1: SIM868.RXI, Raspberry_Pi_3.GPIO14
  N2: SIM868.TXO, Raspberry_Pi_3.GPIO15
  N3: SIM868.POWER, Raspberry_Pi_3.5V
  GND: SIM868.GND, Raspberry_Pi_3.GND, Alarme.pin2, 3-Axis_Accelerometer1.GND
  3V3: Raspberry_Pi_3.3v3, Raspberry_Pi_3.3V3, 3-Axis_Accelerometer1.3.3V
  N4: Raspberry_Pi_3.GPIO2, 3-Axis_Accelerometer1.SDA
  N5: Raspberry_Pi_3.GPIO3, 3-Axis_Accelerometer1.SCL
  N6: Raspberry_Pi_3.GPIO4, R1.Pin_0
  N7: Alarme.pin1, U1.E
  5V: U1.C
