# Fritzing sketch Schema 2 (saved by Fritzing 0.9.3b)

parts:
  Raspberry_Pi_1 = Raspberry Pi 3 [part_number=RPI-3-V1.2]
  Q1 = NPN-Transistor [package="TO92 [THT]"]
  R1 = Resistor [tolerance=±5% resistance=10k package="0402 [SMD]"]
  L1 = Inductor [package="1206 [SMD]"]
  M1 = DC Motor

nets:
  N1: Raspberry_Pi_1.GPIO27, R1.Pin_1
  GND: Raspberry_Pi_1.GND, M1.pin_2
  N2: Q1.E, M1.pin_1
  N3: Q1.B, R1.Pin_0
  N4: Q1.C, L1.pin_1
  5V: L1.pin_0
